# Fritzing sketch ACC_v2 (saved by Fritzing 0.7.0b)
perfboards: 2

parts:
  MainMega = Arduino Mega
  ControllerNano = Arduino Nano v2.3
  MotorNano = Arduino Nano v2.3
  M1 = Stepper Motor - Bipolar
  S1 = H-Bridge with L298N
  Instrument_Cluster_Light_Sensor = Photocell (LDR) [package=THT]
  Part2 = Bluetooth HC-05 Macho
  SwitchedLM = RioRand LM2596
  ConstantLM = RioRand LM2596
  Part3 = LIDAR-Lite_mod
  820uF_25V_Cap = Electrolytic Capacitor [capacitance=0.47mF voltage=20V package="0605 [SMD, electrolytic]"]
  U3 = 4-Channel 5v Relay Shield [package=relay-4ch5v10a]
  Photointerrupter_Resistor1 = Resistor [tolerance=±5% resistance=470 package=THT]
  Photointerrupter_Resistor2 = Resistor [tolerance=±5% resistance=47k package=THT]
  R4 = Resistor [tolerance=±5% resistance=100 package=THT]
  R5 = Resistor [tolerance=±5% resistance=22 package=THT]
  R6 = Resistor [tolerance=±5% resistance=470 package=THT]
  R7 = Resistor [tolerance=±5% resistance=220 package=THT]
  R8 = Resistor [tolerance=±5% resistance=2.2k package=THT]
  Photogate = mystery part, 4 pins [chip_label=? spacing=300mil]
  SteeringWheelMeasure_Resistor = Resistor [tolerance=±5% resistance=1k package=THT]
  CruiseControlLight_Resistor = Resistor [tolerance=±5% resistance=1M package=THT]
  LC_Switch = Round Pushbutton
  Fuzebox_Power = Power plug
  ECU = mystery part, 2 pins [chip_label=? spacing=300mil]
  Steering_Wheel = mystery part, 2 pins [chip_label=? spacing=300mil]
  GY1 = MPU-6050 Board GY-521 [form="♀ (female)" package=THT]
  Photogate1 = mystery part, 4 pins [chip_label=? spacing=300mil]
  Photointerrupter_Resistor3 = Resistor [tolerance=±5% resistance=470 package=THT]
  Photointerrupter_Resistor4 = Resistor [tolerance=±5% resistance=47k package=THT]
  ControllerNano1 = Arduino Nano v2.3  # not connected

nets (from the breadboard view):
  GND: MainMega.GND, MotorNano.GND, S1.GND, Part2.GND, SwitchedLM.Pin_3, Part3.GND, 820uF_25V_Cap.-, Photointerrupter_Resistor2.Pin_0, Photogate.pin1, Photogate1.pin1, Photointerrupter_Resistor4.Pin_0
  N1: MainMega.D3, MotorNano.D9
  N2: MainMega.+5V, CruiseControlLight_Resistor.Pin_0
  VIN: MainMega.VIN, S1.12V, SwitchedLM.Pin_2
  N3: MainMega.A0, Instrument_Cluster_Light_Sensor.pin_0, CruiseControlLight_Resistor.Pin_1
  N4: MainMega.D14, ControllerNano.A5
  N5: MainMega.D15, ControllerNano.A4
  N6: MainMega.D16, Part2.RXD
  N7: MainMega.D17, Part2.TXD
  N8: MainMega.D20, Part3.SDA, GY1.pin4
  N9: MainMega.D21, Part3.SCL, GY1.pin3
  N10: MainMega.A15, MotorNano.D10
  GND_2: ControllerNano.GND, ConstantLM.Pin_3, U3.GND, SteeringWheelMeasure_Resistor.Pin_1, GY1.pin2
  N11: ControllerNano.D4, U3.IN1
  N12: ControllerNano.D5, U3.IN2
  N13: ControllerNano.D6, U3.IN3
  N14: ControllerNano.D7, U3.IN4
  N15: ControllerNano.A1, SteeringWheelMeasure_Resistor.Pin_0, Steering_Wheel.pin1
  VCC: ControllerNano.+5V, Part2.VCC, U3.VCC, Steering_Wheel.pin2, GY1.pin1
  N16: ControllerNano.VIN, ConstantLM.Pin_2
  N17: MotorNano.D3, S1.IN4
  N18: MotorNano.D4, S1.IN3
  N19: MotorNano.D5, S1.IN2
  N20: MotorNano.D6, S1.IN1
  N21: MotorNano.A4, Photogate1.pin2, Photointerrupter_Resistor4.Pin_1
  N22: MotorNano.A3, Photointerrupter_Resistor2.Pin_1, Photogate.pin2
  5V: MotorNano.VIN, S1.5V, Part3.5V, 820uF_25V_Cap.+, Photointerrupter_Resistor1.Pin_1, Photogate.pin3, Photogate1.pin3, Photointerrupter_Resistor3.Pin_1
  N23: M1.A, S1.OUT2-Motor1
  N24: M1.C, S1.OUT1-Motor1
  N25: M1.B, S1.OUT3-Motor2
  N26: M1.D, S1.OUT4-Motor2
  N27: Instrument_Cluster_Light_Sensor.pin_1, SwitchedLM.Pin_1, ConstantLM.Pin_1, Fuzebox_Power.GND
  N28: SwitchedLM.Pin_0, LC_Switch.leg0
  N29: ConstantLM.Pin_0, LC_Switch.leg1, Fuzebox_Power.VCC
  N30: U3.K1-Off, U3.K2-Off, U3.K3-Off, U3.K4-Off, ECU.pin1
  N31: U3.K1-On, R4.Pin_0
  N32: U3.K2-On, R6.Pin_0
  N33: U3.K3-On, R8.Pin_0
  N34: U3.K4-On, R8.Pin_1, ECU.pin2
  N35: Photointerrupter_Resistor1.Pin_0, Photogate.pin4
  N36: R4.Pin_1, R5.Pin_0
  N37: R6.Pin_1, R7.Pin_0
  N38: Photogate1.pin4, Photointerrupter_Resistor3.Pin_0

notes:
  main (back) trigger
  error (front) trigger
  Vertical tube
  Horizontal Tube
  Inside car

custom parts:
  H-Bridge with L298N: h-bridge
  LIDAR-Lite_mod: PulsedLight LIDAR-Lite Sensor
  4-Channel 5v Relay Shield: 4 Channel 5v Relay Shield w. 2x SPD-06VDC-SD-C
  MPU-6050 Board GY-521: Acelerometro y Giroscopio MPU-6050 Board GY-521
